// Logisim project ALU.circ as structural Verilog: 5 circuits, main circuit Adder1b
module Adder8b (
  input  [7:0] in_1,
  input  Cin,
  input  [7:0] in_3,
  output [7:0] out_4,
  output V
);

  wire adder1b_1_cout, adder1b_2_cout, adder1b_3_cout, adder1b_4_cout, adder1b_5_cout, adder1b_6_cout,
       adder1b_7_cout, adder1b_8_cout, xor_1_out, xor_2_out, xor_3_out, xor_4_out, xor_5_out, xor_6_out,
       xor_7_out, xor_8_out;

  xor xor_1 (xor_1_out, Cin, in_3[0]);
  xor xor_2 (xor_2_out, Cin, in_3[1]);
  xor xor_3 (xor_3_out, Cin, in_3[2]);
  xor xor_4 (xor_4_out, Cin, in_3[3]);
  xor xor_5 (xor_5_out, Cin, in_3[4]);
  xor xor_6 (xor_6_out, Cin, in_3[5]);
  xor xor_7 (xor_7_out, Cin, in_3[6]);
  xor xor_8 (xor_8_out, Cin, in_3[7]);
  Adder1b adder1b_1 (.A(in_1[0]), .B(xor_1_out), .S(out_4[0]), .Cin(Cin), .Cout(adder1b_1_cout));
  Adder1b adder1b_2 (.A(in_1[1]), .B(xor_2_out), .S(out_4[1]), .Cin(adder1b_1_cout), .Cout(adder1b_2_cout));
  Adder1b adder1b_3 (.A(in_1[2]), .B(xor_3_out), .S(out_4[2]), .Cin(adder1b_2_cout), .Cout(adder1b_3_cout));
  Adder1b adder1b_4 (.A(in_1[3]), .B(xor_4_out), .S(out_4[3]), .Cin(adder1b_3_cout), .Cout(adder1b_4_cout));
  Adder1b adder1b_5 (.A(in_1[4]), .B(xor_5_out), .S(out_4[4]), .Cin(adder1b_4_cout), .Cout(adder1b_5_cout));
  Adder1b adder1b_6 (.A(in_1[5]), .B(xor_6_out), .S(out_4[5]), .Cin(adder1b_5_cout), .Cout(adder1b_6_cout));
  Adder1b adder1b_7 (.A(in_1[6]), .B(xor_7_out), .S(out_4[6]), .Cin(adder1b_6_cout), .Cout(adder1b_7_cout));
  Adder1b adder1b_8 (.A(in_1[7]), .B(xor_8_out), .S(out_4[7]), .Cin(adder1b_7_cout), .Cout(adder1b_8_cout));
  xor xor_9 (V, adder1b_8_cout, Cin);
endmodule

module Adder1b (
  input  Cin,
  input  A,
  input  B,
  output S,
  output Cout
);

  wire and_1_out, and_2_out, xor_1_out;

  xor xor_1 (xor_1_out, A, B);
  and and_1 (and_1_out, xor_1_out, Cin);
  and and_2 (and_2_out, A, B);
  xor xor_2 (S, xor_1_out, Cin);
  xor xor_3 (Cout, and_1_out, and_2_out);
endmodule

module ALU1b (
  input  SUB,
  input  Cin,
  input  [3:0] AluCtrl,
  input  SrcA,
  input  SrcB,
  output ALURes,
  output N,
  output Z,
  output Cout
);

  wire adder1b_1_cout, adder1b_1_s, adder1b_2_cout, adder1b_2_s, and_1_out, and_2_out, and_3_out, or_1_out,
       or_2_out, xor_1_out, xor_2_out, xor_3_out;

  or or_1 (or_1_out, SUB, Cin);
  and and_1 (and_1_out, SrcA, SrcB);
  or or_2 (or_2_out, SrcA, SrcB);
  xor xor_1 (xor_1_out, SrcA, SrcB);
  xor xor_2 (xor_2_out, SUB, SrcB);
  xor xor_3 (xor_3_out, SrcA, SUB);
  Adder1b adder1b_1 (.A(SrcA), .B(xor_2_out), .S(adder1b_1_s), .Cin(or_1_out), .Cout(adder1b_1_cout));
  and and_2 (and_2_out, adder1b_2_cout, and_3_out);
  or or_3 (Cout, adder1b_1_cout, and_2_out);
  Adder1b adder1b_2 (.A(SrcB), .B(xor_3_out), .S(adder1b_2_s), .Cin(or_1_out), .Cout(adder1b_2_cout));
  Multiplexer #(.select(4)) multiplexer_1 (
    .in0(and_1_out), .in1(xor_1_out), .in2(adder1b_1_s), .in3(adder1b_2_s), .in4(adder1b_1_s),
    .in5(adder1b_1_s), .in6(adder1b_1_s), .in7(adder1b_2_s), .in13(or_2_out), .out(ALURes), .sel(AluCtrl));  // open: in8, in9, in10, in11, in12, in14, in15, en
  and and_3 (and_3_out, SUB, AluCtrl[0]);
  and and_4 (N, SUB, adder1b_1_s);
  not not_1 (Z, adder1b_1_s);

  // Notes on the sheet:
  //   0000 -> AND
  //   0001 -> EOR
  //   0010 -> SUB
  //   0011 -> RSB
  //   0100 -> ADD
  //   0101 -> ADC
  //   0110 -> SBC
  //   0111 -> RSC
  //   1000 -> TST
  //   1001 -> TEQ
  //   1010 -> CMP
  //   1011 -> CMN
  //   1100 -> ORR
  //   1101 -> MOV
  //   1110 -> BIC
  //   1111 -> MVN
endmodule

module ALU8b (
  input  in_1,
  input  in_2,
  input  [3:0] in_3,
  input  [7:0] in_4,
  input  [7:0] in_5,
  output [7:0] out_6,
  output N,
  output Cout,
  output Z
);

  wire alu1b_1_cout, alu1b_1_n, alu1b_1_z, alu1b_2_n, alu1b_2_z, alu1b_3_cout, alu1b_3_n, alu1b_3_z,
       alu1b_4_cout, alu1b_4_n, alu1b_4_z, alu1b_5_cout, alu1b_5_n, alu1b_5_z, alu1b_6_cout, alu1b_6_n,
       alu1b_6_z, alu1b_7_cout, alu1b_7_n, alu1b_7_z, alu1b_8_cout, alu1b_8_n, alu1b_8_z, or_1_out;

  ALU1b alu1b_1 (
    .SrcA(in_4[3]), .SrcB(in_5[3]), .ALURes(out_6[3]), .N(alu1b_1_n), .Z(alu1b_1_z), .Cin(alu1b_3_cout),
    .AluCtrl(in_3), .SUB(in_2), .Cout(alu1b_1_cout));
  ALU1b alu1b_2 (
    .SrcA(in_4[7]), .SrcB(in_5[7]), .ALURes(out_6[7]), .N(alu1b_2_n), .Z(alu1b_2_z), .Cin(alu1b_4_cout),
    .AluCtrl(in_3), .SUB(in_2), .Cout(Cout));
  ALU1b alu1b_3 (
    .SrcA(in_4[2]), .SrcB(in_5[2]), .ALURes(out_6[2]), .N(alu1b_3_n), .Z(alu1b_3_z), .Cin(alu1b_5_cout),
    .AluCtrl(in_3), .SUB(in_2), .Cout(alu1b_3_cout));
  ALU1b alu1b_4 (
    .SrcA(in_4[6]), .SrcB(in_5[6]), .ALURes(out_6[6]), .N(alu1b_4_n), .Z(alu1b_4_z), .Cin(alu1b_6_cout),
    .AluCtrl(in_3), .SUB(in_2), .Cout(alu1b_4_cout));
  ALU1b alu1b_5 (
    .SrcA(in_4[1]), .SrcB(in_5[1]), .ALURes(out_6[1]), .N(alu1b_5_n), .Z(alu1b_5_z), .Cin(alu1b_7_cout),
    .AluCtrl(in_3), .SUB(in_2), .Cout(alu1b_5_cout));
  ALU1b alu1b_6 (
    .SrcA(in_4[5]), .SrcB(in_5[5]), .ALURes(out_6[5]), .N(alu1b_6_n), .Z(alu1b_6_z), .Cin(alu1b_8_cout),
    .AluCtrl(in_3), .SUB(in_2), .Cout(alu1b_6_cout));
  or or_1 (or_1_out, in_1, in_2);
  ALU1b alu1b_7 (
    .SrcA(in_4[0]), .SrcB(in_5[0]), .ALURes(out_6[0]), .N(alu1b_7_n), .Z(alu1b_7_z), .Cin(or_1_out),
    .AluCtrl(in_3), .SUB(in_2), .Cout(alu1b_7_cout));
  ALU1b alu1b_8 (
    .SrcA(in_4[4]), .SrcB(in_5[4]), .ALURes(out_6[4]), .N(alu1b_8_n), .Z(alu1b_8_z), .Cin(alu1b_1_cout),
    .AluCtrl(in_3), .SUB(in_2), .Cout(alu1b_8_cout));
  and and_1 (Z, alu1b_2_z, alu1b_4_z, alu1b_6_z, alu1b_8_z, alu1b_1_z, alu1b_3_z, alu1b_5_z, alu1b_7_z);
  and and_2 (N, alu1b_7_n, alu1b_5_n, alu1b_3_n, alu1b_1_n, alu1b_8_n, alu1b_6_n, alu1b_4_n, alu1b_2_n);
endmodule

module ALU32b (
  input  in_1,
  input  in_2,
  input  [3:0] in_3,
  input  [31:0] in_4,
  input  [31:0] in_5,
  output [31:0] out_6,
  output Z,
  output V
);

  wire alu8b_1_cout, alu8b_1_n, alu8b_1_z, alu8b_2_cout, alu8b_2_n, alu8b_2_z, alu8b_3_cout, alu8b_3_n,
       alu8b_3_z, alu8b_4_n, alu8b_4_z;

  ALU8b alu8b_1 (
    .in_4(in_4[7:0]), .in_5(in_5[7:0]), .out_6(out_6[7:0]), .N(alu8b_1_n), .in_1(in_1), .in_2(in_2),
    .in_3(in_3), .Cout(alu8b_1_cout), .Z(alu8b_1_z));
  ALU8b alu8b_2 (
    .in_4(in_4[15:8]), .in_5(in_5[15:8]), .out_6(out_6[15:8]), .N(alu8b_2_n), .in_1(in_1),
    .in_2(alu8b_1_cout), .in_3(in_3), .Cout(alu8b_2_cout), .Z(alu8b_2_z));
  ALU8b alu8b_3 (
    .in_4(in_4[23:16]), .in_5(in_5[23:16]), .out_6(out_6[23:16]), .N(alu8b_3_n), .in_1(in_1),
    .in_2(alu8b_2_cout), .in_3(in_3), .Cout(alu8b_3_cout), .Z(alu8b_3_z));
  ALU8b alu8b_4 (
    .in_4(in_4[31:24]), .in_5(in_5[31:24]), .out_6(out_6[31:24]), .N(alu8b_4_n), .in_1(in_1),
    .in_2(alu8b_3_cout), .in_3(in_3), .Cout(V), .Z(alu8b_4_z));
  and and_1 (Z, alu8b_1_z, alu8b_2_z, alu8b_3_z, alu8b_4_z);
endmodule
