// Logisim project CPU.circ as structural Verilog: 1 circuit, main circuit main
module main (
  input  Clear
);

  wire and_1_out, BL, clock_1_out, control_unit_1_alusrc, control_unit_1_bic, control_unit_1_branch,
       control_unit_1_c, control_unit_1_memtoreg, control_unit_1_memwrite, control_unit_1_mov,
       control_unit_1_pcsrc, control_unit_1_regwrite, control_unit_1_rs, MOV_or_MVN, MVN, or_1_out;
  wire [1:0] bus_splitter_1_op, control_unit_1_immsrc, control_unit_1_regsrc, TS;
  wire [2:0] control_unit_1_aluctrl;
  wire [3:0] alu_1_nzcv, bus_splitter_1_cond, bus_splitter_1_rd, bus_splitter_1_rm, bus_splitter_1_rn,
       multiplexer_2_out, multiplexer_3_out, multiplexer_4_out;
  wire [4:0] AS;
  wire [5:0] bus_splitter_1_func;
  wire [6:0] bus_splitter_1_shift;
  wire [23:0] bus_splitter_1_imm;
  wire [31:0] adder_1_out, adder_2_out, alu_1_out_5, data_memory_1_data, extends_1_extimm, main_1_out_4,
       multiplexer_1_out, multiplexer_5_out, multiplexer_6_out, multiplexer_7_out, multiplexer_8_out,
       multiplexer_9_out, multiplexer_10_out, multiplexer_11_out, multiplexer_12_out, multiplexer_13_out,
       multiplexer_14_out, multiplexer_15_out, not_1_out, not_2_out, PC_q, register_file_1_rd1,
       register_file_1_rd2, rom_1_data, subtractor_1_out;

  Multiplexer #(.width(32), .enable("false")) multiplexer_1 (
    .in0(adder_1_out), .in1(multiplexer_15_out), .out(multiplexer_1_out), .sel(control_unit_1_pcsrc));
  Clock clock_1 (.out(clock_1_out));
  Register #(.width(32)) PC (.D(multiplexer_1_out), .Q(PC_q), .clk(clock_1_out), .clr(Clear));  // open: en
  ROM #(.addrWidth(24), .dataWidth(32)) rom_1 (.addr(PC_q[25:2]), .data(rom_1_data));  // open: sel
  bus_splitter bus_splitter_1 (
    .in_1(rom_1_data), .Rm(bus_splitter_1_rm), .Rd(bus_splitter_1_rd), .Rn(bus_splitter_1_rn),
    .Func(bus_splitter_1_func), .Op(bus_splitter_1_op), .Cond(bus_splitter_1_cond), .Imm(bus_splitter_1_imm),
    .Shift(bus_splitter_1_shift));
  Adder #(.width(32)) adder_1 (.a(32'h4), .b(PC_q), .out(adder_1_out));  // open: cin, cout
  Adder #(.width(32)) adder_2 (.a(32'h4), .b(adder_1_out), .out(adder_2_out));  // open: cin, cout
  Multiplexer #(.width(4), .enable("false")) multiplexer_2 (
    .in0(bus_splitter_1_rm), .in1(bus_splitter_1_rd), .out(multiplexer_2_out), .sel(control_unit_1_regsrc[1]));
  Control_Unit control_unit_1 (
    .opcode(bus_splitter_1_op), .\function (bus_splitter_1_func), .RD(bus_splitter_1_rd), .NZCV(alu_1_nzcv),
    .CLK(clock_1_out), .COND(bus_splitter_1_cond), .PCSrc(control_unit_1_pcsrc),
    .Branch(control_unit_1_branch), .BL(BL), .ALUSrc(control_unit_1_alusrc), .ImmSrc(control_unit_1_immsrc),
    .RegSrc(control_unit_1_regsrc), .MemWrite(control_unit_1_memwrite), .MOV(control_unit_1_mov), .MVN(MVN),
    .RegWrite(control_unit_1_regwrite), .RS(control_unit_1_rs), .ALUCtrl(control_unit_1_aluctrl),
    .BIC(control_unit_1_bic), .MemtoReg(control_unit_1_memtoreg), .in_5(bus_splitter_1_shift),
    .Type_SHIFT(TS), .SHIFT_AMOUNT(AS), .C(control_unit_1_c));
  Multiplexer #(.width(4), .enable("false")) multiplexer_3 (
    .in0(bus_splitter_1_rn), .in1(4'b1111), .out(multiplexer_3_out), .sel(control_unit_1_regsrc[0]));
  Multiplexer #(.width(4), .enable("false")) multiplexer_4 (
    .in0(bus_splitter_1_rd), .in1(4'b1110), .out(multiplexer_4_out), .sel(BL));
  Multiplexer #(.width(32), .enable("false")) multiplexer_5 (
    .in0(multiplexer_6_out), .in1(adder_2_out), .out(multiplexer_5_out), .sel(BL));
  register_file register_file_1 (
    .CLK(clock_1_out), .WE3(control_unit_1_regwrite), .RST(Clear), .WD3(multiplexer_5_out),
    .A3(multiplexer_4_out), .A2(multiplexer_2_out), .R15(adder_2_out), .RD1(register_file_1_rd1),
    .A1(multiplexer_3_out), .RD2(register_file_1_rd2));
  Extends extends_1 (.ImmSrc(control_unit_1_immsrc), .Imm(bus_splitter_1_imm), .ExtImm(extends_1_extimm));
  Multiplexer #(.width(32), .enable("false")) multiplexer_6 (
    .in0(multiplexer_11_out), .in1(not_1_out), .out(multiplexer_6_out), .sel(MVN));
  or or_1 (or_1_out, control_unit_1_mov, MVN);
  Multiplexer #(.width(32), .enable("false")) multiplexer_7 (
    .in0(register_file_1_rd1), .in1({32{1'b0}}), .out(multiplexer_7_out), .sel(or_1_out));
  Multiplexer #(.width(32), .enable("false")) multiplexer_8 (
    .in0(register_file_1_rd2), .in1(extends_1_extimm), .out(multiplexer_8_out), .sel(control_unit_1_alusrc));
  assign not_1_out = ~multiplexer_11_out;  // NOT_Gate not_1, 32 bits wide
  Multiplexer #(.width(32), .enable("false")) multiplexer_9 (
    .in0(multiplexer_7_out), .in1(multiplexer_8_out), .out(multiplexer_9_out), .sel(control_unit_1_rs));
  Multiplexer #(.width(32), .enable("false")) multiplexer_10 (
    .in0(multiplexer_8_out), .in1(multiplexer_7_out), .out(multiplexer_10_out), .sel(control_unit_1_rs));
  Multiplexer #(.width(32), .enable("false")) multiplexer_11 (
    .in0(multiplexer_15_out), .in1(multiplexer_13_out), .out(multiplexer_11_out), .sel(MOV_or_MVN));
  Multiplexer #(.width(32), .enable("false")) multiplexer_12 (
    .in0(multiplexer_10_out), .in1(not_2_out), .out(multiplexer_12_out), .sel(control_unit_1_bic));
  assign not_2_out = ~multiplexer_10_out;  // NOT_Gate not_2, 32 bits wide
  or or_2 (MOV_or_MVN, control_unit_1_mov, MVN);
  shifter_main main_1 (.in_1(TS), .in_2(multiplexer_12_out), .in_3(AS), .out_4(main_1_out_4));
  Multiplexer #(.width(32), .enable("false")) multiplexer_13 (
    .in0(main_1_out_4), .in1(multiplexer_12_out), .out(multiplexer_13_out), .sel(control_unit_1_alusrc));
  ALU alu_1 (
    .A(multiplexer_9_out), .B(multiplexer_13_out), .out_5(alu_1_out_5), .NZCV(alu_1_nzcv),
    .Cin(control_unit_1_c), .Op(control_unit_1_aluctrl));
  Data_Memory data_memory_1 (
    .A(alu_1_out_5), .WD(register_file_1_rd2), .Data(data_memory_1_data), .WE(control_unit_1_memwrite),
    .RST(Clear), .CLK(clock_1_out));
  Multiplexer #(.width(32), .enable("false")) multiplexer_14 (
    .in0(alu_1_out_5), .in1(data_memory_1_data), .out(multiplexer_14_out), .sel(control_unit_1_memtoreg));
  and and_1 (and_1_out, control_unit_1_pcsrc, ~control_unit_1_branch);  // AND_Gate
  Subtractor #(.width(32)) subtractor_1 (.a(multiplexer_14_out), .b(32'h4), .out(subtractor_1_out));  // open: bin, bout
  Multiplexer #(.width(32), .enable("false")) multiplexer_15 (
    .in0(multiplexer_14_out), .in1(subtractor_1_out), .out(multiplexer_15_out), .sel(and_1_out));

  // Notes on the sheet:
  //   contents of rom_1 (hex, n*v repeats v):
  //   e3a00006 e0800180
endmodule
