// Logisim project CU.circ as structural Verilog: 1 circuit, main circuit Unite de Control
module Unite_de_Control (
  input  [31:0] in_1,
  input  N,
  input  Z,
  input  V,
  input  C,
  output [7:0] \Imm_aprés_rotate ,
  output [3:0] OP_Registre,
  output [3:0] Registre_Dest,
  output [1:0] out_9,
  output _0___Registre___1____Imm,
  output Shift_registre,
  output [4:0] Valeur_Shift,
  output Retour_C,
  output SUB,
  output [3:0] Registre,
  output [3:0] OpCode,
  output [3:0] ConditionCode,
  output Condition_Valide
);

  wire and_1_out, and_3_out, and_4_out, and_5_out, and_6_out, and_7_out, and_8_out, and_9_out, and_10_out,
       and_11_out, and_12_out, and_13_out, and_14_out, and_15_out, and_16_out, and_17_out, C_nZ_out,
       comparator_1_eq, comparator_2_eq, comparator_3_eq, comparator_4_eq, comparator_5_eq, comparator_6_eq,
       comparator_7_eq, comparator_8_eq, comparator_9_eq, comparator_10_eq, comparator_11_eq,
       comparator_12_eq, comparator_13_eq, comparator_14_eq, d_ff_1_q, d_ff_2_q, d_ff_3_q, N__V_out, N_V_out,
       nand_1_out, nand_2_out, nC_Z_out, not_1_out, not_2_out, not_3_out, not_4_out, not_5_out, not_6_out,
       not_7_out, not_8_out, not_9_out, nZ__N_V_out, or_1_out, or_2_out, Z_N__v_out;
  wire [7:0] shifter_1_out;

  and and_1 (and_1_out, ~in_1[24], in_1[21]);  // AND_Gate
  nand nand_1 (nand_1_out, in_1[24], in_1[23]);
  or or_1 (or_1_out, and_1_out, nand_1_out);
  and and_2 (SUB, or_1_out, in_1[22], nand_2_out);
  nand nand_2 (nand_2_out, in_1[24], in_1[21]);
  and and_3 (and_3_out, ~in_1[22], in_1[23], or_2_out);  // AND_Gate
  or or_2 (or_2_out, in_1[22], in_1[21]);
  Transistor #(.gate("br"), .width(4)) transistor_1 (.in(in_1[31:28]), .out(ConditionCode), .gate(not_1_out));
  not not_1 (not_1_out, Condition_Valide);
  D_Flip_Flop d_ff_1 (.clk(in_1[20]), .D(N), .Q(d_ff_1_q));  // open: Qn, preset, en, reset
  D_Flip_Flop d_ff_2 (.clk(in_1[20]), .D(Z), .Q(d_ff_2_q));  // open: Qn, preset, en, reset
  Comparator #(.width(4)) comparator_1 (.a(in_1[31:28]), .b(4'b0000), .eq(comparator_1_eq));  // open: gt, lt
  Comparator #(.width(4)) comparator_2 (.a(in_1[31:28]), .b(4'b0001), .eq(comparator_2_eq));  // open: gt, lt
  Comparator #(.width(4)) comparator_3 (.a(in_1[31:28]), .b(4'b0010), .eq(comparator_3_eq));  // open: gt, lt
  Comparator #(.width(4)) comparator_4 (.a(in_1[31:28]), .b(4'b0011), .eq(comparator_4_eq));  // open: gt, lt
  Comparator #(.width(4)) comparator_5 (.a(in_1[31:28]), .b(4'b0100), .eq(comparator_5_eq));  // open: gt, lt
  Comparator #(.width(4)) comparator_6 (.a(in_1[31:28]), .b(4'b0101), .eq(comparator_6_eq));  // open: gt, lt
  Comparator #(.width(4)) comparator_7 (.a(in_1[31:28]), .b(4'b0110), .eq(comparator_7_eq));  // open: gt, lt
  Comparator #(.width(4)) comparator_8 (.a(in_1[31:28]), .b(4'b0111), .eq(comparator_8_eq));  // open: gt, lt
  D_Flip_Flop d_ff_3 (.clk(in_1[20]), .D(V), .Q(d_ff_3_q));  // open: Qn, preset, en, reset
  not not_2 (not_2_out, d_ff_2_q);
  not not_3 (not_3_out, Retour_C);
  not not_4 (not_4_out, d_ff_1_q);
  not not_5 (not_5_out, d_ff_3_q);
  Transistor #(.width(12)) transistor_2 (
    .in(in_1[11:0]), .out({Valeur_Shift, out_9, Shift_registre, Registre}), .gate(in_1[25]));
  D_Flip_Flop d_ff_4 (.clk(in_1[20]), .D(C), .Q(Retour_C));  // open: Qn, preset, en, reset
  and and_4 (and_4_out, d_ff_2_q, comparator_1_eq);
  and and_5 (and_5_out, not_2_out, comparator_2_eq);
  and and_6 (and_6_out, Retour_C, comparator_3_eq);
  and and_7 (and_7_out, not_3_out, comparator_4_eq);
  and and_8 (and_8_out, d_ff_1_q, comparator_5_eq);
  and and_9 (and_9_out, not_4_out, comparator_6_eq);
  and and_10 (and_10_out, d_ff_3_q, comparator_7_eq);
  and and_11 (and_11_out, not_5_out, comparator_8_eq);
  not not_6 (not_6_out, d_ff_2_q);
  and C_nZ (C_nZ_out, Retour_C, not_6_out);
  not not_7 (not_7_out, Retour_C);
  and nC_Z (nC_Z_out, not_7_out, d_ff_2_q);
  xnor N_V (N_V_out, d_ff_1_q, d_ff_3_q);
  Comparator #(.width(4)) comparator_9 (.a(4'b1101), .b(in_1[31:28]), .eq(comparator_9_eq));  // open: gt, lt
  Comparator #(.width(4)) comparator_10 (.a(4'b1100), .b(in_1[31:28]), .eq(comparator_10_eq));  // open: gt, lt
  Comparator #(.width(4)) comparator_11 (.a(4'b1011), .b(in_1[31:28]), .eq(comparator_11_eq));  // open: gt, lt
  Comparator #(.width(4)) comparator_12 (.a(4'b1010), .b(in_1[31:28]), .eq(comparator_12_eq));  // open: gt, lt
  Comparator #(.width(4)) comparator_13 (.a(4'b1001), .b(in_1[31:28]), .eq(comparator_13_eq));  // open: gt, lt
  Comparator #(.width(4)) comparator_14 (.a(4'b1000), .b(in_1[31:28]), .eq(comparator_14_eq));  // open: gt, lt
  xor N__V (N__V_out, d_ff_1_q, d_ff_3_q);
  not not_8 (not_8_out, d_ff_2_q);
  and nZ__N_V (nZ__N_V_out, not_8_out, N_V_out);
  or Z_N__v (Z_N__v_out, d_ff_2_q, N__V_out);
  Shifter #(.shift("rr")) shifter_1 (.in(in_1[7:0]), .\dist (in_1[10:8]), .out(shifter_1_out));
  not not_9 (not_9_out, in_1[25]);
  Transistor #(.width(8)) transistor_3 (.in(shifter_1_out), .out(\Imm_aprés_rotate ), .gate(not_9_out));
  and and_12 (and_12_out, Z_N__v_out, comparator_9_eq);
  and and_13 (and_13_out, nZ__N_V_out, comparator_10_eq);
  and and_14 (and_14_out, N__V_out, comparator_11_eq);
  and and_15 (and_15_out, N_V_out, comparator_12_eq);
  and and_16 (and_16_out, nC_Z_out, comparator_13_eq);
  and and_17 (and_17_out, C_nZ_out, comparator_14_eq);
  or or_3 (Condition_Valide, and_4_out, and_5_out, and_6_out, and_7_out, and_8_out, and_9_out, and_10_out, and_11_out, and_12_out, and_13_out, and_14_out, and_15_out, and_16_out, and_17_out);

  assign _0___Registre___1____Imm = in_1[25];
  assign OP_Registre = in_1[19:16];
  assign OpCode = in_1[24:21];
  assign Registre_Dest = in_1[15:12];

  // Notes on the sheet:
  //   1000 -> HI
  //   1001 -> LS
  //   1010 -> GE
  //   1011 -> LT
  //   1100 -> GT
  //   1101 ->LE
  //   1110 -> AL
  //   CARRY FLAG
  //   0000 -> EQ
  //   0001 -> NE
  //   0010 -> CS
  //   0011 -> CC
  //   0100 -> MI
  //   0101 -> PL
  //   0110 -> VS
  //   0111 -> VC
  //   0000 -> AND
  //   0001 -> EOR
  //   0010 -> SUB
  //   0011 -> RSB
  //   0100 -> ADD
  //   0101 -> ADC
  //   0110 -> SBC
  //   1000 -> TST
  //   1001 -> TEQ
  //   1100 -> ORR
  //   0111 -> RSC
  //   1110 -> BIC
  //   1010 -> CMP
  //   1011 -> CMN
  //   1101 -> MOV
  //   1111 -> MVN
  //   00 -> logical left
  //   01 -> logical right
  //   10 -> arithmetic right
  //   11 -> rotate right
endmodule
