// Logisim project DataMemory.circ as structural Verilog: 1 circuit, main circuit Data Memory
module Data_Memory (
  input  [31:0] Addresse,
  input  [31:0] Donnee,
  input  Store,
  input  Clock,
  input  Load,
  input  Clear,
  output [31:0] Donnee_2
);

  RAM #(.addrWidth(24), .dataWidth(32), .bus("separate")) ram_1 (
    .addr(Addresse[25:2]), .din(Donnee), .data(Donnee_2), .str(Store), .sel(1'b1), .clk(Clock), .ld(Load),
    .clr(Clear));
endmodule
