// Logisim project MemInstr.circ as structural Verilog: 1 circuit, main circuit main
module main (
  input  Addresse_ou_PC,
  input  [7:0] Addresse_Selection,
  output [31:0] out_3
);

  wire clock_1_out;
  wire [7:0] counter_1_q, multiplexer_1_out;

  Multiplexer #(.width(8)) multiplexer_1 (
    .in0(Addresse_Selection), .in1(counter_1_q), .out(multiplexer_1_out), .sel(Addresse_ou_PC));  // open: en
  Clock clock_1 (.out(clock_1_out));
  Counter counter_1 (.D(multiplexer_1_out), .Q(counter_1_q), .clk(clock_1_out));  // open: load, count, carry, clr
  RAM #(.dataWidth(32)) ram_1 (.addr(multiplexer_1_out), .data(out_3), .sel(1'b1));  // open: clk, ld, clr

  // Notes on the sheet:
  //   Faire load image et importer fichier binaire
endmodule
