// Logisim project alu.circ as structural Verilog: 1 circuit, main circuit main
module main (
  input  Cin,
  input  [2:0] Op,
  input  [31:0] A,
  input  [31:0] B,
  output [31:0] out_5,
  output [3:0] NZVC
);

  wire adder_1_cout, and_2_out, and_3_out, nor_1_out, subtractor_1_bout;
  wire [31:0] adder_1_out, and_1_out, or_1_out, subtractor_1_out, xor_1_out;

  Adder #(.width(32)) adder_1 (.a(A), .b(B), .out(adder_1_out), .cin(Cin), .cout(adder_1_cout));
  Subtractor #(.width(32)) subtractor_1 (.a(A), .b(B), .out(subtractor_1_out), .bin(Cin), .bout(subtractor_1_bout));
  assign and_1_out = A & B;  // AND_Gate and_1, 32 bits wide
  assign or_1_out = A | B;  // OR_Gate or_1, 32 bits wide
  assign xor_1_out = A ^ B;  // XOR_Gate xor_1, 32 bits wide
  and and_2 (and_2_out, ~Op[2], ~Op[1], Op[0]);  // AND_Gate
  Multiplexer #(.select(3), .width(32)) multiplexer_1 (
    .in0(adder_1_out), .in1(subtractor_1_out), .in2(and_1_out), .in3(or_1_out), .in4(xor_1_out),
    .in5({32{1'b0}}), .in6({32{1'b0}}), .in7({32{1'b0}}), .out({NZVC[3], out_5[30:0]}), .sel(Op));  // open: en
  Multiplexer multiplexer_2 (.in0(adder_1_cout), .in1(subtractor_1_bout), .out(NZVC[0]), .sel(and_2_out));  // open: en
  and and_3 (and_3_out, A[31], B[31]);
  xor xor_2 (NZVC[1], NZVC[3], and_3_out);
  // Probe on nor_1_out
  nor nor_1 (nor_1_out, out_5[0], out_5[1], out_5[2], out_5[3], out_5[4], out_5[5], out_5[6], out_5[7], out_5[8], out_5[9], out_5[10], out_5[11], out_5[12], out_5[13], out_5[14], out_5[15], out_5[16], out_5[17], out_5[18], out_5[19], out_5[20], out_5[21], out_5[22], out_5[23], out_5[24], out_5[25], out_5[26], out_5[27], out_5[28], out_5[29], out_5[30], NZVC[3]);
  and and_4 (NZVC[2], ~NZVC[0], nor_1_out);  // AND_Gate

  assign out_5[31] = NZVC[3];
endmodule
