// Logisim project bus_splitter.circ as structural Verilog: 1 circuit, main circuit bus_splitter
module bus_splitter (
  input  [31:0] in_1,
  output [3:0] Rm,
  output [6:0] Shift,
  output [3:0] Rd,
  output [3:0] Rn,
  output [5:0] Func,
  output [1:0] Op,
  output [3:0] Cond,
  output [23:0] Imm
);


  assign Cond = in_1[31:28];
  assign Func = in_1[25:20];
  assign Imm = in_1[23:0];
  assign Op = in_1[27:26];
  assign Rd = in_1[15:12];
  assign Rm = in_1[3:0];
  assign Rn = in_1[19:16];
  assign Shift = in_1[11:5];
endmodule
