// Logisim project control_unit.circ as structural Verilog: 1 circuit, main circuit Control_Unit
module Control_Unit (
  input  [1:0] opcode,
  input  [5:0] \function ,
  input  [3:0] RD,
  input  [3:0] NZCV,
  input  [6:0] in_5,
  input  CLK,
  input  [3:0] COND,
  output PCSrc,
  output Branch,
  output BL,
  output ALUSrc,
  output MemtoReg,
  output [1:0] ImmSrc,
  output [1:0] RegSrc,
  output MemWrite,
  output MOV,
  output MVN,
  output RegWrite,
  output RS,
  output [2:0] ALUCtrl,
  output BIC,
  output [1:0] Type_SHIFT,
  output [4:0] SHIFT_AMOUNT,
  output C
);

  wire ADD_out, AL_out, and_2_out, and_3_out, and_4_out, and_5_out, and_9_out, and_10_out, and_11_out,
       and_12_out, AND_out, C_t, CC_out, CMN_out, CMP_out, CS_out, DP_Imm_out, DP_REG_out, EOR_out, EQ_out,
       GE_out, GT_out, HI_out, LE_out, LS_out, LT_out, MI_out, NE_out, or_4_out, or_5_out, or_8_out,
       or_11_out, or_12_out, or_13_out, or_14_out, or_16_out, or_17_out, or_18_out, OR_out, PL_out,
       register_1_q, register_2_q, register_3_q, register_4_q, STR_out, SUB_out, TEQ_out, TST_out, VC_out,
       VS_out, xnor_1_out;

  and u_Branch (ImmSrc[1], opcode[1], ~opcode[0]);  // AND_Gate
  and B_Link (BL, opcode[1], \function [4], ~opcode[0]);  // AND_Gate
  and LDR (MemtoReg, ~opcode[1], opcode[0], \function [0]);  // AND_Gate
  and STR (STR_out, ~opcode[1], opcode[0], ~\function [0]);  // AND_Gate
  and DP_REG (DP_REG_out, ~opcode[1], ~opcode[0], ~\function [5]);  // AND_Gate
  and DP_Imm (DP_Imm_out, ~opcode[1], ~opcode[0], \function [5]);  // AND_Gate
  and ADD (ADD_out, or_4_out, ~\function [4], \function [3], ~\function [2]);  // AND_Gate
  and SUB (SUB_out, or_4_out, ~\function [4], \function [2]);  // AND_Gate
  and AND (AND_out, or_4_out, ~\function [4], ~\function [3], ~\function [2], ~\function [1]);  // AND_Gate
  and OR (OR_out, or_4_out, \function [4], \function [3], ~\function [2], ~\function [1]);  // AND_Gate
  and EOR (EOR_out, or_4_out, ~\function [4], ~\function [3], ~\function [2], \function [1]);  // AND_Gate
  and CMP (CMP_out, or_4_out, \function [4], ~\function [3], \function [2], ~\function [1], \function [0]);  // AND_Gate
  and CMN (CMN_out, or_4_out, \function [0], ~\function [4], \function [3], \function [2], \function [1]);  // AND_Gate
  and TST (TST_out, or_4_out, \function [0], \function [4], ~\function [3], ~\function [2], ~\function [1]);  // AND_Gate
  and TEQ (TEQ_out, or_4_out, \function [0], \function [4], ~\function [3], ~\function [2], \function [1]);  // AND_Gate
  and u_BIC (BIC, or_4_out, \function [4], \function [3], \function [2], ~\function [1]);  // AND_Gate
  or or_2 (Branch, ImmSrc[1], BL);
  or or_3 (ImmSrc[0], MemtoReg, STR_out);
  or or_4 (or_4_out, DP_REG_out, DP_Imm_out);
  and and_2 (and_2_out, ADD_out, \function [1]);
  and and_3 (and_3_out, SUB_out, \function [3]);
  and and_4 (and_4_out, RD[0], RD[1], RD[2], RD[3]);
  and and_5 (and_5_out, ImmSrc[0], \function [5]);
  or or_5 (or_5_out, BL, MemtoReg, or_4_out);
  and and_6 (MOV, or_4_out, \function [1], ~\function [2], \function [3], \function [4]);  // AND_Gate
  and and_7 (MVN, or_4_out, \function [1], \function [2], \function [3], \function [4]);
  and and_8 (RS, SUB_out, \function [1]);
  or or_6 (ALUCtrl[1], AND_out, TST_out, BIC, OR_out);
  or or_7 (ALUCtrl[0], SUB_out, OR_out, CMP_out);
  or or_8 (or_8_out, ADD_out, BIC, SUB_out);
  and and_9 (and_9_out, \function [3], RS);
  or or_9 (ALUCtrl[2], EOR_out, TEQ_out);
  and and_10 (and_10_out, and_4_out, or_5_out);
  // Probe on or_4_out
  or or_10 (ALUSrc, and_5_out, ImmSrc[1], DP_Imm_out);
  or or_11 (or_11_out, CMP_out, CMN_out, TST_out, TEQ_out);
  and and_11 (and_11_out, or_8_out, \function [0]);
  or or_12 (or_12_out, and_10_out, Branch);
  or or_13 (or_13_out, STR_out, ImmSrc[1]);
  or or_14 (or_14_out, and_11_out, or_11_out);
  and and_12 (and_12_out, \function [0], CLK);
  or or_15 (C_t, and_2_out, and_9_out, and_3_out);
  Register #(.width(1)) register_1 (.D(NZCV[0]), .Q(register_1_q), .clk(and_12_out), .clr(or_14_out));  // open: en
  and and_13 (PCSrc, or_12_out, or_18_out);
  and and_14 (RegWrite, or_5_out, or_18_out, ~or_11_out);  // AND_Gate
  Register #(.width(1)) register_2 (.D(NZCV[1]), .Q(register_2_q), .clk(and_12_out), .clr(or_14_out));  // open: en
  and and_15 (MemWrite, or_13_out, or_18_out);
  Register #(.width(1)) register_3 (.D(NZCV[2]), .Q(register_3_q), .clk(and_12_out));  // open: en, clr
  Register #(.width(1)) register_4 (.D(NZCV[3]), .Q(register_4_q), .clk(and_12_out));  // open: en, clr
  and EQ (EQ_out, ~COND[0], ~COND[1], ~COND[2], ~COND[3], register_3_q);  // AND_Gate
  and NE (NE_out, COND[0], ~COND[1], ~COND[2], ~COND[3], ~register_3_q);  // AND_Gate
  and CS (CS_out, ~COND[0], COND[1], ~COND[2], ~COND[3], register_2_q);  // AND_Gate
  and CC (CC_out, COND[0], COND[1], ~COND[2], ~COND[3], ~register_2_q);  // AND_Gate
  and MI (MI_out, ~COND[0], ~COND[1], COND[2], ~COND[3], register_4_q);  // AND_Gate
  and PL (PL_out, COND[0], ~COND[1], COND[2], ~COND[3], ~register_4_q);  // AND_Gate
  and VS (VS_out, ~COND[0], COND[1], COND[2], ~COND[3], register_1_q);  // AND_Gate
  and VC (VC_out, COND[0], COND[1], COND[2], ~COND[3], ~register_1_q);  // AND_Gate
  xnor xnor_1 (xnor_1_out, register_1_q, register_4_q);
  and and_16 (C, register_2_q, C_t);
  and GT (GT_out, ~COND[0], ~COND[1], COND[2], COND[3], ~register_3_q, xnor_1_out);  // AND_Gate
  and LT (LT_out, COND[0], COND[1], ~COND[2], COND[3], ~xnor_1_out);  // AND_Gate
  and GE (GE_out, ~COND[0], COND[1], ~COND[2], COND[3], xnor_1_out);  // AND_Gate
  or or_16 (or_16_out, ~xnor_1_out, register_3_q);  // OR_Gate
  and HI (HI_out, ~COND[0], ~COND[1], ~COND[2], ~COND[3], register_2_q, ~register_3_q);  // AND_Gate
  or or_17 (or_17_out, ~register_2_q, register_3_q);  // OR_Gate
  and AL (AL_out, ~COND[0], COND[1], COND[2], COND[3]);  // AND_Gate
  and LE (LE_out, COND[0], ~COND[1], COND[2], COND[3], or_16_out);  // AND_Gate
  and LS (LS_out, COND[0], ~COND[1], ~COND[2], COND[3], or_17_out);  // AND_Gate
  or or_18 (or_18_out, EQ_out, NE_out, CS_out, CC_out, MI_out, PL_out, VS_out, VC_out, GT_out, LT_out, GE_out, LE_out, HI_out, LS_out, AL_out);

  assign RegSrc = {ImmSrc[0], ImmSrc[1]};
  assign SHIFT_AMOUNT = in_5[6:2];
  assign Type_SHIFT = in_5[1:0];
endmodule
