// Logisim project data_memory.circ as structural Verilog: 1 circuit, main circuit Data Memory
module Data_Memory (
  input  [31:0] A,
  input  [31:0] WD,
  input  CLK,
  input  RST,
  input  WE,
  output [31:0] Data
);

  wire not_1_out;

  RAM #(.addrWidth(24), .dataWidth(32), .bus("separate")) ram_1 (
    .addr(A[25:2]), .din(WD), .data(Data), .str(WE), .sel(1'b1), .clk(CLK), .ld(not_1_out), .clr(RST));
  not not_1 (not_1_out, WE);
endmodule
