// Logisim project extend_immediate.circ as structural Verilog: 1 circuit, main circuit Extends
module Extends (
  input  [1:0] ImmSrc,
  input  [23:0] Imm,
  output [31:0] ExtImm
);

  wire [7:0] bit_extender_3_out;
  wire [11:0] bit_extender_4_out;
  wire [23:0] demultiplexer_1_out0, demultiplexer_1_out1, demultiplexer_1_out2;
  wire [25:0] bit_extender_1_out, shifter_1_out;
  wire [31:0] bit_extender_2_out, bit_extender_5_out, bit_extender_6_out;

  Demultiplexer #(.select(2), .width(24), .enable("false")) demultiplexer_1 (
    .out0(demultiplexer_1_out0), .out1(demultiplexer_1_out1), .out2(demultiplexer_1_out2), .in(Imm),
    .sel(ImmSrc));  // open: out3
  assign bit_extender_1_out = {{2{1'b0}}, demultiplexer_1_out2};  // Bit_Extender bit_extender_1
  Shifter #(.width(26)) shifter_1 (.in(bit_extender_1_out), .\dist (5'b00010), .out(shifter_1_out));
  assign bit_extender_2_out = {{6{shifter_1_out[25]}}, shifter_1_out};  // Bit_Extender bit_extender_2
  Bit_Extender #(.in_width(24), .out_width(8)) bit_extender_3 (.in(demultiplexer_1_out0), .out(bit_extender_3_out));
  Bit_Extender #(.in_width(24), .out_width(12)) bit_extender_4 (.in(demultiplexer_1_out1), .out(bit_extender_4_out));
  // Probe on bit_extender_2_out
  assign bit_extender_5_out = {{24{1'b0}}, bit_extender_3_out};  // Bit_Extender bit_extender_5
  assign bit_extender_6_out = {{20{1'b0}}, bit_extender_4_out};  // Bit_Extender bit_extender_6
  // Probe on bit_extender_5_out
  // Probe on bit_extender_6_out
  Multiplexer #(.select(2), .width(32), .enable("false")) multiplexer_1 (
    .in0(bit_extender_5_out), .in1(bit_extender_6_out), .in2(bit_extender_2_out), .out(ExtImm), .sel(ImmSrc));  // open: in3
endmodule
