// Logisim project register_file.circ as structural Verilog: 1 circuit, main circuit register_file
module register_file (
  input  CLK,
  input  WE3,
  input  RST,
  input  [31:0] WD3,
  input  [3:0] A1,
  input  [3:0] A3,
  input  [3:0] A2,
  input  [31:0] R15,
  output [31:0] RD1,
  output [31:0] RD2
);

  wire and_1_out, and_2_out, and_3_out, and_4_out, and_5_out, and_6_out, and_7_out, and_8_out, and_9_out,
       and_10_out, and_11_out, and_12_out, and_13_out, and_14_out, and_15_out, decoder_1_out0,
       decoder_1_out1, decoder_1_out2, decoder_1_out3, decoder_1_out4, decoder_1_out5, decoder_1_out6,
       decoder_1_out7, decoder_1_out8, decoder_1_out9, decoder_1_out10, decoder_1_out11, decoder_1_out12,
       decoder_1_out13, decoder_1_out14, decoder_1_out15;
  wire [31:0] R0_q, R1_q, R2_q, R3_q, R4_q, R5_q, R6_q, R7_q, R8_q, R9_q, R10_q, R11_q, R12_q, R13_q, R14_q,
       R15_q;

  Decoder #(.select(4)) decoder_1 (
    .out0(decoder_1_out0), .out1(decoder_1_out1), .out2(decoder_1_out2), .out3(decoder_1_out3),
    .out4(decoder_1_out4), .out5(decoder_1_out5), .out6(decoder_1_out6), .out7(decoder_1_out7),
    .out8(decoder_1_out8), .out9(decoder_1_out9), .out10(decoder_1_out10), .out11(decoder_1_out11),
    .out12(decoder_1_out12), .out13(decoder_1_out13), .out14(decoder_1_out14), .out15(decoder_1_out15),
    .sel(A3));  // open: en
  and and_1 (and_1_out, WE3, decoder_1_out0);
  and and_2 (and_2_out, WE3, decoder_1_out1);
  and and_3 (and_3_out, WE3, decoder_1_out2);
  and and_4 (and_4_out, WE3, decoder_1_out3);
  and and_5 (and_5_out, WE3, decoder_1_out4);
  and and_6 (and_6_out, WE3, decoder_1_out5);
  and and_7 (and_7_out, WE3, decoder_1_out6);
  and and_8 (and_8_out, WE3, decoder_1_out7);
  and and_9 (and_9_out, WE3, decoder_1_out8);
  and and_10 (and_10_out, WE3, decoder_1_out9);
  and and_11 (and_11_out, WE3, decoder_1_out10);
  and and_12 (and_12_out, WE3, decoder_1_out11);
  and and_13 (and_13_out, WE3, decoder_1_out12);
  and and_14 (and_14_out, WE3, decoder_1_out13);
  and and_15 (and_15_out, WE3, decoder_1_out14);
  Register #(.width(32)) R0 (.D(WD3), .en(and_1_out), .Q(R0_q), .clk(CLK), .clr(RST));
  Register #(.width(32)) R1 (.D(WD3), .en(and_2_out), .Q(R1_q), .clk(CLK), .clr(RST));
  Register #(.width(32)) R2 (.D(WD3), .en(and_3_out), .Q(R2_q), .clk(CLK), .clr(RST));
  Register #(.width(32)) R3 (.D(WD3), .en(and_4_out), .Q(R3_q), .clk(CLK), .clr(RST));
  Register #(.width(32)) R4 (.D(WD3), .en(and_5_out), .Q(R4_q), .clk(CLK), .clr(RST));
  Register #(.width(32)) R5 (.D(WD3), .en(and_6_out), .Q(R5_q), .clk(CLK), .clr(RST));
  Register #(.width(32)) R6 (.D(WD3), .en(and_7_out), .Q(R6_q), .clk(CLK), .clr(RST));
  Register #(.width(32)) R7 (.D(WD3), .en(and_8_out), .Q(R7_q), .clk(CLK), .clr(RST));
  Register #(.width(32)) R8 (.D(WD3), .en(and_9_out), .Q(R8_q), .clk(CLK), .clr(RST));
  Register #(.width(32)) R9 (.D(WD3), .en(and_10_out), .Q(R9_q), .clk(CLK), .clr(RST));
  Register #(.width(32)) R10 (.D(WD3), .en(and_11_out), .Q(R10_q), .clk(CLK), .clr(RST));
  Register #(.width(32)) R11 (.D(WD3), .en(and_12_out), .Q(R11_q), .clk(CLK), .clr(RST));
  Register #(.width(32)) R12 (.D(WD3), .en(and_13_out), .Q(R12_q), .clk(CLK), .clr(RST));
  Register #(.width(32)) R13 (.D(WD3), .en(and_14_out), .Q(R13_q), .clk(CLK), .clr(RST));
  Register #(.width(32)) R14 (.D(WD3), .en(and_15_out), .Q(R14_q), .clk(CLK), .clr(RST));
  Register #(.width(32)) u_R15 (.D(R15), .en(decoder_1_out15), .Q(R15_q), .clk(CLK), .clr(RST));
  // Probe on R0_q
  // Probe on R1_q
  // Probe on R9_q
  // Probe on R8_q
  // Probe on R2_q
  // Probe on R10_q
  // Probe on R4_q
  // Probe on R3_q
  // Probe on R11_q
  // Probe on R12_q
  // Probe on R5_q
  // Probe on R13_q
  // Probe on R6_q
  // Probe on R7_q
  // Probe on R15_q
  // Probe on R14_q
  Multiplexer #(.select(4), .width(32)) multiplexer_1 (
    .in0(R0_q), .in1(R1_q), .in2(R2_q), .in3(R3_q), .in4(R4_q), .in5(R5_q), .in6(R6_q), .in7(R7_q),
    .in8(R8_q), .in9(R9_q), .in10(R10_q), .in11(R11_q), .in12(R12_q), .in13(R13_q), .in14(R14_q),
    .in15(R15_q), .out(RD2), .sel(A2));  // open: en
  Multiplexer #(.select(4), .width(32)) multiplexer_2 (
    .in0(R0_q), .in1(R1_q), .in2(R2_q), .in3(R3_q), .in4(R4_q), .in5(R5_q), .in6(R6_q), .in7(R7_q),
    .in8(R8_q), .in9(R9_q), .in10(R10_q), .in11(R11_q), .in12(R12_q), .in13(R13_q), .in14(R14_q),
    .in15(R15_q), .out(RD1), .sel(A1));  // open: en
endmodule
